// Logisim project RGLED-第1关.circ as structural Verilog: 17 circuits, main circuit LED计数测试
// LED计数
module \LED计数电路  (
  input  In1,
  input  In2,
  input  In3,
  input  In4,
  input  In5,
  output Out1,
  output Out2,
  output Out3,
  output Out4,
  output Out5
);

  or or_1 (Out1, In1, In2, In3, In4, In5);
  or or_2 (Out2, In2, In3, In4, In5);
  or or_3 (Out3, In3, In4, In5);
  or or_4 (Out4, In4, In5);

  assign Out5 = In5;
endmodule

module \LED计数测试  (
);

  wire _1_out, _2_out, _3_out, _4_out, _5_out, \数码管驱动_1_seg_1 , \数码管驱动_1_seg_2 , \数码管驱动_1_seg_3 ,
       \数码管驱动_1_seg_4 , \数码管驱动_1_seg_5 , \数码管驱动_1_seg_6 , \数码管驱动_1_seg_7 , \计数电路_out1 , \计数电路_out2 ,
       \计数电路_out3 , \计数电路_out4 , \计数电路_out5 ;
  wire [2:0] \n5输入编码器_1_out1 ;

  Button _1 (.out(_1_out));
  Button _2 (.out(_2_out));
  Button _3 (.out(_3_out));
  Button _4 (.out(_4_out));
  Button _5 (.out(_5_out));
  \LED计数电路  \u_计数电路  (
    .In1(_1_out), .Out1(\计数电路_out1 ), .In2(_2_out), .Out2(\计数电路_out2 ), .In5(_5_out), .Out5(\计数电路_out5 ),
    .Out3(\计数电路_out3 ), .Out4(\计数电路_out4 ), .In3(_3_out), .In4(_4_out));
  \_5输入编码器  \u_5输入编码器_1  (
    .In1(_1_out), .Out1(\n5输入编码器_1_out1 [0]), .In2(_2_out), .In3(_3_out), .In4(_4_out),
    .Out2(\n5输入编码器_1_out1 [1]), .In5(_5_out), .Out3(\n5输入编码器_1_out1 [2]));
  // Probe on \n5输入编码器_1_out1 
  Hex_Digit_Display hex_digit_display_1 (.value({1'b0, \n5输入编码器_1_out1 }), .dp(1'b1));
  \数码管驱动  \u_数码管驱动_1  (
    .X3(1'b0), .X2(\n5输入编码器_1_out1 [2]), .X1(\n5输入编码器_1_out1 [1]), .Seg_1(\数码管驱动_1_seg_1 ),
    .X0(\n5输入编码器_1_out1 [0]), .Seg_2(\数码管驱动_1_seg_2 ), .Seg_3(\数码管驱动_1_seg_3 ), .Seg_4(\数码管驱动_1_seg_4 ),
    .Seg_5(\数码管驱动_1_seg_5 ), .Seg_6(\数码管驱动_1_seg_6 ), .Seg_7(\数码管驱动_1_seg_7 ));
  _7_Segment_Display #(.active("true")) u_7_segment_display_1 (
    .g(\数码管驱动_1_seg_1 ), .f(\数码管驱动_1_seg_2 ), .a(\数码管驱动_1_seg_3 ), .b(\数码管驱动_1_seg_4 ), .e(\数码管驱动_1_seg_5 ),
    .d(\数码管驱动_1_seg_6 ), .c(\数码管驱动_1_seg_7 ));  // open: dp
  _7_Segment_Display #(.active("true")) u_7_segment_display_2 ();  // open: g, f, a, b, e, d, c, dp

  // Notes on the sheet:
  //   16进制显示
  //   7段管显示
endmodule

// 编码器
module \_5输入编码器  (
  input  In1,
  input  In2,
  input  In3,
  input  In4,
  input  In5,
  output Out1,
  output Out2,
  output Out3
);

  wire and_1_out, and_2_out, and_3_out, and_4_out, not_1_out, not_2_out, not_3_out, not_4_out, not_5_out,
       not_6_out, not_7_out, not_8_out;

  not not_1 (not_1_out, In4);
  not not_2 (not_2_out, In2);
  not not_3 (not_3_out, In4);
  not not_4 (not_4_out, In4);
  not not_5 (not_5_out, In5);
  not not_6 (not_6_out, In3);
  not not_7 (not_7_out, In4);
  not not_8 (not_8_out, In5);
  or or_1 (Out3, In5, In4);
  and and_1 (and_1_out, In3, not_1_out);
  and and_2 (and_2_out, In1, not_2_out, not_3_out);
  and and_3 (and_3_out, In3, not_4_out, not_5_out);
  and and_4 (and_4_out, In2, not_6_out, not_7_out, not_8_out);
  or or_2 (Out1, In5, and_1_out, and_2_out);
  or or_3 (Out2, and_3_out, and_4_out);
endmodule

module \数码管驱动  (
  input  X3,
  input  X2,
  input  X1,
  input  X0,
  output Seg_1,
  output Seg_2,
  output Seg_3,
  output Seg_4,
  output Seg_5,
  output Seg_6,
  output Seg_7
);

  wire and_1_out, and_2_out, and_3_out, and_4_out, and_5_out, and_6_out, and_7_out, and_8_out, and_9_out,
       and_10_out, and_11_out, and_12_out, and_13_out, and_14_out, and_15_out, and_16_out, and_17_out,
       and_18_out, and_19_out, and_20_out, and_21_out, and_22_out, and_23_out, and_24_out, and_25_out,
       and_26_out, and_27_out, and_28_out, and_29_out, and_30_out, and_31_out, and_32_out, and_33_out,
       and_34_out, and_35_out, not_1_out, not_2_out, not_3_out, not_4_out, not_5_out, not_6_out, not_7_out,
       not_8_out, not_9_out, not_10_out, not_11_out, not_12_out, not_13_out, not_14_out, not_15_out,
       not_16_out, not_17_out, not_18_out, not_19_out, not_20_out, not_21_out, not_22_out, not_23_out,
       not_24_out, not_25_out, not_26_out, not_27_out, not_28_out, not_29_out, not_30_out, not_31_out,
       not_32_out, not_33_out, not_34_out, not_35_out, not_36_out, not_37_out, not_38_out, not_39_out,
       not_40_out, not_41_out, not_42_out, not_43_out, not_44_out;

  not not_1 (not_1_out, X2);
  and and_1 (and_1_out, not_1_out, X1);
  and and_2 (and_2_out, X1, not_2_out);
  not not_2 (not_2_out, X0);
  not not_3 (not_3_out, X3);
  and and_3 (and_3_out, not_3_out, X2, not_4_out);
  not not_4 (not_4_out, X1);
  and and_4 (and_4_out, X3, not_5_out);
  not not_5 (not_5_out, X2);
  and and_5 (and_5_out, X3, X0);
  not not_6 (not_6_out, X1);
  and and_6 (and_6_out, not_6_out, not_7_out);
  not not_7 (not_7_out, X0);
  not not_8 (not_8_out, X3);
  and and_7 (and_7_out, not_8_out, X2, not_9_out);
  not not_9 (not_9_out, X1);
  and and_8 (and_8_out, X2, not_10_out);
  not not_10 (not_10_out, X0);
  and and_9 (and_9_out, X3, not_11_out);
  not not_11 (not_11_out, X2);
  and and_10 (and_10_out, X3, X1);
  not not_12 (not_12_out, X2);
  and and_11 (and_11_out, not_12_out, not_13_out);
  not not_13 (not_13_out, X0);
  not not_14 (not_14_out, X3);
  and and_12 (and_12_out, not_14_out, X1);
  not not_15 (not_15_out, X3);
  and and_13 (and_13_out, not_15_out, X2, X0);
  and and_14 (and_14_out, X2, X1);
  not not_16 (not_16_out, X2);
  and and_15 (and_15_out, X3, not_16_out, not_17_out);
  not not_17 (not_17_out, X1);
  and and_16 (and_16_out, X3, not_18_out);
  not not_18 (not_18_out, X0);
  not not_19 (not_19_out, X3);
  and and_17 (and_17_out, not_19_out, not_20_out);
  not not_20 (not_20_out, X2);
  not not_21 (not_21_out, X3);
  not not_22 (not_22_out, X1);
  and and_18 (and_18_out, not_21_out, not_22_out, not_23_out);
  not not_23 (not_23_out, X0);
  not not_24 (not_24_out, X2);
  and and_19 (and_19_out, not_24_out, not_25_out);
  not not_25 (not_25_out, X0);
  not not_26 (not_26_out, X3);
  and and_20 (and_20_out, not_26_out, X1, X0);
  and and_21 (and_21_out, X3, not_27_out, X0);
  not not_27 (not_27_out, X1);
  not not_28 (not_28_out, X2);
  and and_22 (and_22_out, not_28_out, not_29_out);
  not not_29 (not_29_out, X0);
  and and_23 (and_23_out, X1, not_30_out);
  not not_30 (not_30_out, X0);
  and and_24 (and_24_out, X3, X1);
  and and_25 (and_25_out, X3, X2);
  not not_31 (not_31_out, X3);
  not not_32 (not_32_out, X2);
  and and_26 (and_26_out, not_31_out, not_32_out, not_33_out);
  not not_33 (not_33_out, X0);
  not not_34 (not_34_out, X2);
  and and_27 (and_27_out, not_34_out, X1, X0);
  and and_28 (and_28_out, X2, not_35_out, X0);
  not not_35 (not_35_out, X1);
  and and_29 (and_29_out, X2, X1, not_36_out);
  not not_36 (not_36_out, X0);
  and and_30 (and_30_out, X3, not_37_out, not_38_out);
  not not_37 (not_37_out, X1);
  not not_38 (not_38_out, X0);
  not not_39 (not_39_out, X3);
  and and_31 (and_31_out, not_39_out, not_40_out);
  not not_40 (not_40_out, X1);
  not not_41 (not_41_out, X3);
  and and_32 (and_32_out, not_41_out, X0);
  not not_42 (not_42_out, X1);
  and and_33 (and_33_out, not_42_out, X0);
  not not_43 (not_43_out, X3);
  and and_34 (and_34_out, not_43_out, X2);
  and and_35 (and_35_out, X3, not_44_out);
  not not_44 (not_44_out, X2);
  or or_1 (Seg_1, and_1_out, and_2_out, and_3_out, and_4_out, and_5_out);
  or or_2 (Seg_2, and_6_out, and_7_out, and_8_out, and_9_out, and_10_out);
  or or_3 (Seg_4, and_17_out, and_18_out, and_19_out, and_20_out, and_21_out);
  or or_4 (Seg_5, and_22_out, and_23_out, and_24_out, and_25_out);
  or or_5 (Seg_6, and_26_out, and_27_out, and_28_out, and_29_out, and_30_out);
  or or_6 (Seg_7, and_31_out, and_32_out, and_33_out, and_34_out, and_35_out);
  or or_7 (Seg_3, and_11_out, and_12_out, and_13_out, and_14_out, and_15_out, and_16_out);
endmodule

module \数码管驱动测试  (
);

  wire clock_1_out, \数码管驱动_1_seg_1 , \数码管驱动_1_seg_2 , \数码管驱动_1_seg_3 , \数码管驱动_1_seg_4 , \数码管驱动_1_seg_5 ,
       \数码管驱动_1_seg_6 , \数码管驱动_1_seg_7 ;
  wire [3:0] counter_1_q;

  Counter #(.width(4), .max('hf), .ongoal("wrap"), .trigger("rising"), .behavior("old")) counter_1 (
    .Q(counter_1_q), .clk(clock_1_out));  // open: load, D, count, carry, clr, preset
  Clock #(.highDuration(1), .lowDuration(1)) clock_1 (.out(clock_1_out));
  // Probe on counter_1_q
  \数码管驱动  \u_数码管驱动_1  (
    .X3(counter_1_q[3]), .X2(counter_1_q[2]), .X1(counter_1_q[1]), .Seg_1(\数码管驱动_1_seg_1 ),
    .X0(counter_1_q[0]), .Seg_2(\数码管驱动_1_seg_2 ), .Seg_3(\数码管驱动_1_seg_3 ), .Seg_4(\数码管驱动_1_seg_4 ),
    .Seg_5(\数码管驱动_1_seg_5 ), .Seg_6(\数码管驱动_1_seg_6 ), .Seg_7(\数码管驱动_1_seg_7 ));
  _7_Segment_Display #(.active("true")) u_7_segment_display_1 (
    .g(\数码管驱动_1_seg_1 ), .f(\数码管驱动_1_seg_2 ), .a(\数码管驱动_1_seg_3 ), .b(\数码管驱动_1_seg_4 ), .e(\数码管驱动_1_seg_5 ),
    .d(\数码管驱动_1_seg_6 ), .c(\数码管驱动_1_seg_7 ));  // open: dp
endmodule

// 4位数比较器
module \_4位无符号比较器  (
  input  X3,
  input  X2,
  input  X1,
  input  X0,
  input  Y3,
  input  Y2,
  input  Y1,
  input  Y0,
  output Great,
  output Equal,
  output Less
);
endmodule

module \_8位无符号比较器  (
  input  [7:0] X,
  input  [7:0] Y,
  output Great,
  output Equal,
  output Less
);

  // Probe on X
  // Probe on Y
  \_4位无符号比较器  \u_4位无符号比较器_1  ();  // open: X3, X2, X1, X0, Y3, Y2, Y1, Y0, Great, Equal, Less
  \_4位无符号比较器  \u_4位无符号比较器_2  ();  // open: X3, X2, X1, X0, Y3, Y2, Y1, Y0, Great, Equal, Less

  // Other names for the same wires on the sheet: X0[3:0] = X[3:0]; X1[3:0] = X[7:4]; Y0[3:0] = Y[3:0];
  //   Y1[3:0] = Y[7:4]

  // Notes on the sheet:
  //   电路功能：X,Y进行无符号比较，Great=(X>Y)?1:0;
  //   输入引脚区
  //   输出引脚区
endmodule

// MUX
module \_2路选择器_1位  (
  input  X0,
  input  Sel,
  input  X1,
  output Out
);


  // Notes on the sheet:
  //   输入引脚区
  //   电路功能：Out=(Sel==0)?X0:X1;
  //   请勿增删改引脚，请在下方利用上方输入输出引脚的隧道标签信号构建电路，ctrl+d复制选择组件
  //   输出引脚区
endmodule

// MUX
module \_2路选择器_8位  (
  input  [7:0] X,
  input  Sel,
  input  [7:0] Y,
  output [7:0] Out
);

  // Probe on X
  // Probe on Y
  // Probe on Out

  // Notes on the sheet:
  //   输入引脚区
  //   电路功能：Out=(Sel==0)?X:Y;
  //   请勿增删改引脚，请在下方利用上方输入输出引脚的隧道标签信号构建电路，ctrl+d复制选择组件
  //   输出引脚区
endmodule

// 计数器
module \BCD双向计数器_可异步置位  (
  input  CLK,
  input  \使能 ,
  input  \异步置位控制 ,
  input  [3:0] \异步预置 ,
  input  \Mode_1正计数_0倒计数 ,
  output [3:0] \输出Q ,
  output \进位_借位 
);

  wire D0, D1, D2, D3, undriven;

  \BCD双向计数器状态转换_自动生成  \bcd双向计数器状态转换_自动生成_1  ();  // open: S3, N3, S2, N2, S1, N1, S0, N0, Mode
  \BCD双向计数器输出函数_自动生成  \bcd双向计数器输出函数_自动生成_1  (.Cout(\进位_借位 ));  // open: S3, S2, S1, S0, Mode
  assign {D3, D2, D1, D0} = \异步置位控制  ? \异步预置  : 4'bz;  // Controlled_Buffer controlled_buffer_1
  D_Flip_Flop #(.trigger("rising"), .Pre_Clr_Positions("LEGACY"), .NegatePresetClear("false"), .enable("true"), .NewFFLayout("false")) u_D3 ();  // open: clk, D, Q, Qn, preset, en, reset
  D_Flip_Flop #(.trigger("rising"), .Pre_Clr_Positions("LEGACY"), .NegatePresetClear("false"), .enable("true"), .NewFFLayout("false")) u_D2 ();  // open: clk, D, Q, Qn, preset, en, reset
  D_Flip_Flop #(.trigger("rising"), .Pre_Clr_Positions("LEGACY"), .NegatePresetClear("false"), .enable("true"), .NewFFLayout("false")) u_D1 (.reset(undriven));  // open: clk, D, Q, Qn, preset, en
  D_Flip_Flop #(.trigger("rising"), .Pre_Clr_Positions("LEGACY"), .NegatePresetClear("false"), .enable("true"), .NewFFLayout("false")) u_D0 ();  // open: clk, D, Q, Qn, preset, en, reset
  // Probe on \输出Q 

  // Other names for the same wires on the sheet: Cout = \进位_借位 ; Din[3:0] = \异步预置 ; En = \使能 ;
  //   Mode = \Mode_1正计数_0倒计数 ; PreSet = \异步置位控制 ; Q[3:0] = \输出Q 

  // Notes on the sheet:
  //   正计数到9，倒计数到0时输出为1
endmodule

// 状态转换
module \BCD双向计数器状态转换_自动生成  (
  input  S3,
  input  S2,
  input  S1,
  input  S0,
  input  Mode,
  output N3,
  output N2,
  output N1,
  output N0
);
endmodule

module \BCD双向计数器输出函数_自动生成  (
  input  S3,
  input  S2,
  input  S1,
  input  S0,
  input  Mode,
  output Cout
);
endmodule

// 倒计数
module \双位十进制双向计数器  (
  input  CLK,
  input  \使能 ,
  input  \异步置位控制 ,
  input  [7:0] \异步预置 ,
  input  \Mode_1正计数_0倒计数 ,
  output [7:0] Q,
  output \进位_借位 
);

  \BCD双向计数器_可异步置位  \bcd双向计数器_可异步置位_1  ();  // open: CLK, 使能, 异步置位控制, 异步预置, Mode_1正计数_0倒计数, 输出Q, 进位_借位
  \BCD双向计数器_可异步置位  \bcd双向计数器_可异步置位_2  ();  // open: CLK, 使能, 异步置位控制, 异步预置, Mode_1正计数_0倒计数, 输出Q, 进位_借位
  // Probe on Q

  // Other names for the same wires on the sheet: Cout = \进位_借位 ; Din[7:0] = \异步预置 ; Din0[3:0] = \异步预置 [3:0];
  //   Din1[3:0] = \异步预置 [7:4]; En = \使能 ; Mode = \Mode_1正计数_0倒计数 ; PreSet = \异步置位控制 

  // Notes on the sheet:
  //   正计数到9，倒计数到0时输出为1
endmodule

// 状态机
module \红绿灯状态机_自动生成  (
  input  S2,
  input  S1,
  input  S0,
  input  T1,
  input  T2,
  input  T3,
  input  T4,
  input  EMERG,
  output N2,
  output N1,
  output N0
);
endmodule

// 输出函数
module \红绿灯状态输出函数_真值表  (
  input  S2,
  input  S1,
  input  S0,
  output R1,
  output Y1,
  output G1,
  output R2,
  output Y2,
  output G2,
  output PASS1,
  output PASS2
);
endmodule

module \红绿灯  (
  input  in_1,
  output R1,
  output Y1,
  output [2:0] Status,
  output G1,
  output R2,
  output Y2,
  output [7:0] Timer,
  output G2
);

  wire CLK, PASS1, RST, T1, T2, undriven_2, Y1c, Y2c, \紧急开关_p1 , \紧急开关_p3 , \紧急开关_p7 , \紧急情况 ;
  wire [2:0] S1B, S2B;
  wire [3:0] S1T, S2T;
  wire [7:0] counter_1_q, Timer1, undriven;

  LED #(.active("true")) led_1 (.in(R1));
  LED #(.active("true")) led_2 (.in(Y1c));
  LED #(.active("true")) led_3 (.in(G1));
  _7_Segment_Display #(.active("true")) u_7_segment_display_1 (
    .g(S1T[0]), .f(S1T[1]), .a(S1T[2]), .b(S1T[3]), .e(S1B[0]), .d(S1B[1]), .c(S1B[2]));  // open: dp
  _7_Segment_Display #(.active("true")) u_7_segment_display_2 (
    .g(S2T[0]), .f(S2T[1]), .a(S2T[2]), .b(S2T[3]), .e(S2B[0]), .d(S2B[1]), .c(S2B[2]));  // open: dp
  Register #(.width(3), .trigger("rising"), .Select("low")) \u_状态  (.Q(Status), .clk(CLK));  // open: D, en, clr
  \双位十进制双向计数器  \u_双位十进制双向计数器_1  (
    .CLK(CLK), .\使能 (1'b1), .\异步预置 (8'h20), .Q(Timer1));  // open: 异步置位控制, Mode_1正计数_0倒计数, 进位_借位
  // DipSwitch #(.NSwitches(1)) 紧急开关: pin names not known; wires that end beside it: \紧急开关_p1 , \紧急开关_p1 , \紧急开关_p3 , R1, Y1, G1, \紧急开关_p7 , \紧急开关_p7 , R2, Y2, G2, PASS1
  \红绿灯状态输出函数_真值表  \u_红绿灯状态输出函数_真值表_1  ();  // open: S2, R1, S1, Y1, S0, G1, R2, Y2, G2, PASS1, PASS2
  // Probe on Timer1
  LED #(.active("true")) led_4 (.in(R2));
  LED #(.active("true")) led_5 (.in(Y2c));
  LED #(.active("true")) led_6 (.in(G2));
  or or_1 (\紧急情况 , in_1, \紧急开关_p3 );
  \红绿灯状态机_自动生成  \u_红绿灯状态机_自动生成_1  ();  // open: S2, N2, S1, N1, S0, N0, T1, T2, T3, T4, EMERG
  \_8位无符号比较器  \u_8位无符号比较器_1  (.X(Timer1), .Y(8'h4), .Equal(T1));  // open: Great, Less
  \_8位无符号比较器  \u_8位无符号比较器_2  (.X(Timer1), .Y(8'h1), .Equal(T2));  // open: Great, Less
  and and_1 (Y1c, Y1, CLK);
  and and_2 (Y2c, Y2, CLK);
  Clock #(.highDuration(1), .lowDuration(1)) clock_1 (.out(CLK));
  \_2路选择器_8位  \u_2路选择器_8位_1  (.X(Timer1), .Sel(undriven_2), .Y(undriven), .Out(Timer));
  D_Flip_Flop #(.trigger("rising"), .Pre_Clr_Positions("LEGACY"), .NegatePresetClear("false"), .enable("true"), .NewFFLayout("false")) d_ff_1 (
    .clk(CLK), .D(1'b1), .Qn(RST));  // open: Q, preset, en, reset
  Counter #(.width(8), .max('hff), .ongoal("wrap"), .trigger("rising"), .behavior("new")) counter_1 (
    .Q(counter_1_q), .clk(CLK));  // open: load, D, count, carry, clr, preset, down
  // Probe on counter_1_q
  \数码管驱动  \u_数码管驱动_1  (
    .X3(Timer[7]), .X2(Timer[6]), .X1(Timer[5]), .Seg_1(S2T[0]), .X0(Timer[4]), .Seg_2(S2T[1]),
    .Seg_3(S2T[2]), .Seg_4(S2T[3]), .Seg_5(S2B[0]), .Seg_6(S2B[1]), .Seg_7(S2B[2]));
  \数码管驱动  \u_数码管驱动_2  (
    .X3(Timer[3]), .X2(Timer[2]), .X1(Timer[1]), .Seg_1(S1T[0]), .X0(Timer[0]), .Seg_2(S1T[1]),
    .Seg_3(S1T[2]), .Seg_4(S1T[3]), .Seg_5(S1B[0]), .Seg_6(S1B[1]), .Seg_7(S1B[2]));

  // Other names for the same wires on the sheet: E = in_1

  // Notes on the sheet:
  //   主道红绿灯
  //   测试时要求主道20秒，辅道10秒
  //   倒计时
  //   状态机现态
  //   主道计时逻辑
  //   辅道红绿灯
  //   状态机现态
  //   当前倒计时
  //   引脚区，用于EduCoder测试
  //   控制黄灯闪烁
  //   初始化信号，第一拍为1
  //   用于预置计数器初始值
  //   当前倒计时
  //   时钟计数
endmodule

module _11_17experiment (
  input  in_1,
  input  in_2,
  input  in_3,
  input  in_4,
  input  in_5
);

  wire \led计数电路_1_out1 , \led计数电路_1_out2 , \led计数电路_1_out3 , \led计数电路_1_out4 , \led计数电路_1_out5 ;

  \LED计数电路  \led计数电路_1  (
    .In1(in_1), .Out1(\led计数电路_1_out1 ), .In2(in_2), .Out2(\led计数电路_1_out2 ), .In5(in_5),
    .Out5(\led计数电路_1_out5 ), .Out3(\led计数电路_1_out3 ), .Out4(\led计数电路_1_out4 ), .In3(in_3), .In4(in_4));
  LED #(.active("true")) led_1 (.in(\led计数电路_1_out1 ));
  LED #(.active("true")) led_2 (.in(\led计数电路_1_out2 ));
  LED #(.active("true")) led_3 (.in(\led计数电路_1_out3 ));
  LED #(.active("true")) led_4 (.in(\led计数电路_1_out4 ));
  LED #(.active("true")) led_5 (.in(\led计数电路_1_out5 ));
endmodule
