// Logisim project 全加器.circ as structural Verilog: 2 circuits, main circuit 一位全加器
module \一位全加器  (
  input  d1,
  input  d2,
  input  f_l,
  output o1,
  output o_h
);

  wire and_1_out, and_2_out, and_3_out, and_4_out, and_5_out, and_6_out, and_7_out, and_8_out, and_9_out,
       and_10_out, and_11_out, not_1_out, not_2_out, not_3_out, not_4_out, not_5_out, not_6_out, or_1_out,
       or_3_out, or_4_out;

  not not_1 (not_1_out, d1);
  not not_2 (not_2_out, d2);
  not not_3 (not_3_out, d1);
  not not_4 (not_4_out, d2);
  and and_1 (and_1_out, d2, f_l);
  and and_2 (and_2_out, d1, f_l);
  and and_3 (and_3_out, not_1_out, not_2_out);
  and and_4 (and_4_out, not_3_out, d2);
  not not_5 (not_5_out, f_l);
  and and_5 (and_5_out, d1, not_4_out);
  not not_6 (not_6_out, f_l);
  and and_6 (and_6_out, d1, d2);
  or or_1 (or_1_out, and_1_out, and_2_out);
  and and_7 (and_7_out, d1, d2);
  and and_8 (and_8_out, and_3_out, f_l);
  and and_9 (and_9_out, and_4_out, not_5_out);
  and and_10 (and_10_out, and_5_out, not_6_out);
  and and_11 (and_11_out, and_6_out, f_l);
  or or_2 (o_h, or_1_out, and_7_out);
  or or_3 (or_3_out, and_8_out, and_9_out);
  or or_4 (or_4_out, and_10_out, and_11_out);
  or or_5 (o1, or_3_out, or_4_out);
endmodule

module \全加器串联  (
  input  [7:0] in_1,
  input  [7:0] in_2,
  output [7:0] out_3
);

  wire \一位全加器_1_o_h , \一位全加器_2_o_h , \一位全加器_3_o_h , \一位全加器_4_o_h , \一位全加器_5_o_h , \一位全加器_6_o_h ,
       \一位全加器_7_o_h ;

  \一位全加器  \u_一位全加器_1  (.d1(in_1[0]), .d2(in_2[0]), .f_l(1'b0), .o1(out_3[0]), .o_h(\一位全加器_1_o_h ));
  \一位全加器  \u_一位全加器_2  (.d1(in_1[1]), .d2(in_2[1]), .f_l(\一位全加器_1_o_h ), .o1(out_3[1]), .o_h(\一位全加器_2_o_h ));
  \一位全加器  \u_一位全加器_3  (.d1(in_1[2]), .d2(in_2[2]), .f_l(\一位全加器_2_o_h ), .o1(out_3[2]), .o_h(\一位全加器_3_o_h ));
  \一位全加器  \u_一位全加器_4  (.d1(in_1[4]), .d2(in_2[4]), .f_l(\一位全加器_5_o_h ), .o1(out_3[4]), .o_h(\一位全加器_4_o_h ));
  \一位全加器  \u_一位全加器_5  (.d1(in_1[3]), .d2(in_2[3]), .f_l(\一位全加器_3_o_h ), .o1(out_3[3]), .o_h(\一位全加器_5_o_h ));
  \一位全加器  \u_一位全加器_6  (.d1(in_1[5]), .d2(in_2[5]), .f_l(\一位全加器_4_o_h ), .o1(out_3[5]), .o_h(\一位全加器_6_o_h ));
  \一位全加器  \u_一位全加器_7  (.d1(in_1[6]), .d2(in_2[6]), .f_l(\一位全加器_6_o_h ), .o1(out_3[6]), .o_h(\一位全加器_7_o_h ));
  \一位全加器  \u_一位全加器_8  (.d1(in_1[7]), .d2(in_2[7]), .f_l(\一位全加器_7_o_h ), .o1(out_3[7]));  // open: o_h
endmodule
