// Logisim project 移码.circ as structural Verilog: 1 circuit, main circuit main
module main (
  input  [4:0] in_1,
  output [4:0] out_2
);

  wire and_1_out, and_2_out, and_3_out, xor_2_out, xor_4_out, xor_6_out, xor_7_out;

  xor xor_1 (out_2[3], and_1_out, xor_2_out);
  not not_1 (out_2[4], in_1[4]);
  xor xor_2 (xor_2_out, in_1[4], in_1[3]);
  and and_1 (and_1_out, and_2_out, xor_4_out);
  xor xor_3 (out_2[2], and_2_out, xor_4_out);
  xor xor_4 (xor_4_out, in_1[4], in_1[2]);
  and and_2 (and_2_out, and_3_out, xor_6_out);
  xor xor_5 (out_2[1], and_3_out, xor_6_out);
  xor xor_6 (xor_6_out, in_1[4], in_1[1]);
  xor xor_7 (xor_7_out, in_1[4], in_1[0]);
  xor xor_8 (out_2[0], in_1[4], xor_7_out);
  and and_3 (and_3_out, in_1[4], xor_7_out);
endmodule
